// Logisim project cam314_lab6.circ as structural Verilog: 2 circuits, main circuit main
module main (
);

  wire CLK, Kout, not_1_out;
  wire [3:0] adder_1_out, Counter_q;
  wire [7:0] _0s_q, _1s_q, adder_2_out, adder_3_out;

  Clock clock_1 (.out(CLK));
  Register #(.width(4)) Counter (.D(adder_1_out), .Q(Counter_q), .clk(CLK));  // open: en, clr
  Adder #(.width(4)) adder_1 (.a(Counter_q), .b(4'b0001), .out(adder_1_out));  // open: cin, cout
  kmap kmap_1 (.A(Counter_q[0]), .B(Counter_q[1]), .C(Counter_q[2]), .D(Counter_q[3]), .Q(Kout));
  Register _1s (.D(adder_2_out), .en(Kout), .Q(_1s_q), .clk(CLK));  // open: clr
  Register _0s (.D(adder_3_out), .en(not_1_out), .Q(_0s_q), .clk(CLK));  // open: clr
  not not_1 (not_1_out, Kout);
  Adder adder_2 (.a(_1s_q), .b(8'h1), .out(adder_2_out));  // open: cin, cout
  Adder adder_3 (.a(_0s_q), .b(8'h1), .out(adder_3_out));  // open: cin, cout
endmodule

module kmap (
  input  A,
  input  B,
  input  C,
  input  D,
  output Q
);

  wire A_prime_C_prime_out, B_prime_C_prime_out, B_prime_D_prime_out, BD_out, not_1_out, not_2_out,
       not_3_out, not_4_out, not_5_out, not_6_out;

  not not_1 (not_1_out, A);
  not not_2 (not_2_out, C);
  not not_3 (not_3_out, B);
  not not_4 (not_4_out, C);
  not not_5 (not_5_out, B);
  not not_6 (not_6_out, D);
  and A_prime_C_prime (A_prime_C_prime_out, not_1_out, not_2_out);
  and BD (BD_out, B, D);
  and B_prime_C_prime (B_prime_C_prime_out, not_3_out, not_4_out);
  and B_prime_D_prime (B_prime_D_prime_out, not_5_out, not_6_out);
  or or_1 (Q, A_prime_C_prime_out, BD_out, B_prime_C_prime_out, B_prime_D_prime_out);
endmodule
