// Logisim project cam314_lab8.circ as structural Verilog: 2 circuits, main circuit main
module main (
);

  Register_File register_file_1 ();  // open: Clock, Data, Write_Enable, rd, rs, rt, incr7, decr7, rs_out, rt_out

  // Notes on the sheet:
  //   See "Register File" subcircuit
endmodule

module Register_File (
  input  Clock,
  input  [15:0] Data,
  input  Write_Enable,
  input  [2:0] rd,
  input  [2:0] rs,
  input  [2:0] rt,
  input  incr7,
  input  decr7,
  output [15:0] rs_out,
  output [15:0] rt_out
);

  wire or_1_out, WE0, WE1, WE2, WE3, WE4, WE5, WE6, WE7;
  wire [15:0] adder_1_out, multiplexer_1_out, multiplexer_2_out, reg0, reg1, reg2, reg3, reg4, reg5, reg6,
       reg7, register_8_q, subtractor_1_out, subtractor_2_out;

  Demultiplexer #(.select(3)) demultiplexer_1 (
    .out0(WE0), .out1(WE1), .out2(WE2), .out3(WE3), .out4(WE4), .out5(WE5), .out6(WE6), .out7(WE7),
    .in(Write_Enable), .sel(rd));  // open: en
  Adder #(.width(16)) adder_1 (.a(register_8_q), .b(16'h1), .out(adder_1_out));  // open: cin, cout
  Multiplexer #(.width(16)) multiplexer_1 (
    .in0(Data), .in1(adder_1_out), .out(multiplexer_1_out), .sel(incr7));  // open: en
  Subtractor #(.width(16)) subtractor_1 (.a(register_8_q), .b(16'h1), .out(subtractor_1_out));  // open: bin, bout
  Multiplexer #(.width(16)) multiplexer_2 (
    .in0(multiplexer_1_out), .in1(subtractor_1_out), .out(multiplexer_2_out), .sel(decr7));  // open: en
  or or_1 (or_1_out, incr7, decr7, WE7);
  Register #(.width(16)) register_1 (.D(Data), .en(WE0), .Q(reg0), .clk(Clock));  // open: clr
  Register #(.width(16)) register_2 (.D(Data), .en(WE1), .Q(reg1), .clk(Clock));  // open: clr
  Register #(.width(16)) register_3 (.D(Data), .en(WE2), .Q(reg2), .clk(Clock));  // open: clr
  Register #(.width(16)) register_4 (.D(Data), .en(WE3), .Q(reg3), .clk(Clock));  // open: clr
  Register #(.width(16)) register_5 (.D(Data), .en(WE4), .Q(reg4), .clk(Clock));  // open: clr
  Register #(.width(16)) register_6 (.D(Data), .en(WE5), .Q(reg5), .clk(Clock));  // open: clr
  Register #(.width(16)) register_7 (.D(Data), .en(WE6), .Q(reg6), .clk(Clock));  // open: clr
  Register #(.width(16)) register_8 (.D(multiplexer_2_out), .en(or_1_out), .Q(register_8_q), .clk(Clock));  // open: clr
  Multiplexer #(.width(16)) multiplexer_3 (
    .in0(register_8_q), .in1(subtractor_2_out), .out(reg7), .sel(decr7));  // open: en
  Subtractor #(.width(16)) subtractor_2 (.a(register_8_q), .b(16'h1), .out(subtractor_2_out));  // open: bin, bout
  Multiplexer #(.select(3), .width(16)) multiplexer_4 (
    .in0(reg0), .in1(reg1), .in2(reg2), .in3(reg3), .in4(reg4), .in5(reg5), .in6(reg6), .in7(reg7),
    .out(rs_out), .sel(rs));  // open: en
  Multiplexer #(.select(3), .width(16)) multiplexer_5 (
    .in0(reg0), .in1(reg1), .in2(reg2), .in3(reg3), .in4(reg4), .in5(reg5), .in6(reg6), .in7(reg7),
    .out(rt_out), .sel(rt));  // open: en
endmodule
