// Logisim project cam314.circ as structural Verilog: 6 circuits, main circuit main
module main (
);

  wire clear, CLK, D_WE, decr7, halt, i_type, incr7, mac, N, RAM_str, RF_WE, Signed, Z;
  wire [1:0] PCSrc;
  wire [2:0] ALUop, b_Type, rd, RDS, rs, rt;
  wire [3:0] Display_d1, Display_d2, Display_d3, Display_d4;
  wire [7:0] imm;
  wire [15:0] ALU_res, bit_extender_1_out, bit_extender_2_out, bit_extender_3_out, high, mfhi, mflo,
       multiplexer_1_out, multiplexer_2_out, multiplexer_4_out, PC_pc, r7, RAM_out, rd_out, rom_1_data,
       rs_out, rt_out;
  wire [31:0] adder_1_out, multiplexer_3_out;

  PC PC (
    .Halt(halt), .j_target(rs_out), .immediate(imm), .N_flag(N), .Z_flag(Z), .branchType(b_Type),
    .Clock(CLK), .PCSrc(PCSrc), .rd(rd), .PC(PC_pc));  // open: PC_1
  assign bit_extender_1_out = {{8{1'b0}}, imm};  // Bit_Extender bit_extender_1
  Multiplexer #(.select(3), .width(16)) multiplexer_1 (
    .in0(ALU_res), .in1(bit_extender_1_out), .in2({imm, rd_out[7:0]}), .in3(rs_out), .in4(mfhi), .in5(mflo),
    .in6(RAM_out), .out(multiplexer_1_out), .sel(RDS));  // open: in7, en
  ROM #(.addrWidth(16), .dataWidth(16)) rom_1 (.addr(PC_pc), .data(rom_1_data));  // open: sel
  Register_File Reg_File (
    .Data(multiplexer_1_out), .Clock(CLK), .I_Type(i_type), .incr7(incr7), .decr7(decr7),
    .Write_Enable(RF_WE), .rd(rd), .rs(rs), .rt(rt), .rs_out(rs_out), .rt_out(rt_out), .rd_out(rd_out),
    .r7(r7));
  Control control_1 (
    .ROM_out(rom_1_data), .i_type(i_type), .rd(rd), .rs(rs), .rt(rt), .imm(imm), .Signed(Signed),
    .ALUop(ALUop), .RegFile_WE(RF_WE), .PCSrc(PCSrc), .BranchType(b_Type), .RDS(RDS), .RAM_str(RAM_str),
    .halt(halt), .put(D_WE), .clr(clear), .mac(mac), .decr7(decr7), .incr7(incr7));  // open: li, lui, mov, mfhi, mflo, pop
  assign bit_extender_2_out = {{8{1'b0}}, imm};  // Bit_Extender bit_extender_2
  assign bit_extender_3_out = {{8{imm[7]}}, imm};  // Bit_Extender bit_extender_3
  Adder #(.width(32)) adder_1 (.a({high, ALU_res}), .b({mfhi, mflo}), .out(adder_1_out));  // open: cin, cout
  Multiplexer #(.width(16)) multiplexer_2 (
    .in0(bit_extender_2_out), .in1(bit_extender_3_out), .out(multiplexer_2_out), .sel(Signed));  // open: en
  Clock clock_1 (.out(CLK));
  LED u_HALT (.in(halt));
  Display Display (
    .Data(rs_out), .Write_Enable(D_WE), .Clear(clear), .Clock(CLK), .D1(Display_d1), .D2(Display_d2),
    .D3(Display_d3), .D4(Display_d4));
  RAM #(.addrWidth(16), .dataWidth(16), .bus("separate")) ram_1 (
    .addr(rs_out), .din(rt_out), .data(RAM_out), .str(RAM_str), .clk(CLK));  // open: sel, ld, clr
  Register #(.width(32)) Product (.D(multiplexer_3_out), .Q({mfhi, mflo}), .clk(CLK));  // open: en, clr
  Multiplexer #(.width(32)) multiplexer_3 (
    .in0({high, ALU_res}), .in1(adder_1_out), .out(multiplexer_3_out), .sel(mac));  // open: en
  ALU ALU (
    .Input_A(rs_out), .Input_B(multiplexer_4_out), .ALUop(ALUop), .Result(ALU_res), .High(high), .Z_flag(Z),
    .N_flag(N));
  Multiplexer #(.width(16)) multiplexer_4 (
    .in0(rt_out), .in1(multiplexer_2_out), .out(multiplexer_4_out), .sel(i_type));  // open: en
  Hex_Digit_Display hex_digit_display_1 (.value(Display_d1));  // open: dp
  Hex_Digit_Display hex_digit_display_2 (.value(Display_d2));  // open: dp
  Hex_Digit_Display hex_digit_display_3 (.value(Display_d3));  // open: dp
  Hex_Digit_Display hex_digit_display_4 (.value(Display_d4));  // open: dp

  // Notes on the sheet:
  //   contents of rom_1 (hex, n*v repeats v):
  //   8568 8ef0 8779 8df1 1a08 800 200 a00 200 8050 80a1 1a08 a02 280 1c08 a02 280
endmodule

module Display (
  input  [15:0] Data,
  input  Write_Enable,
  input  Clear,
  input  Clock,
  output [3:0] D1,
  output [3:0] D2,
  output [3:0] D3,
  output [3:0] D4
);

  wire or_1_out;
  wire [15:0] multiplexer_1_out;

  Multiplexer #(.width(16)) multiplexer_1 (
    .in0(Data), .in1({16{1'b0}}), .out(multiplexer_1_out), .sel(Clear));  // open: en
  or or_1 (or_1_out, Clear, Write_Enable);
  Register #(.width(16)) register_1 (
    .D(multiplexer_1_out), .en(or_1_out), .Q({D1, D2, D3, D4}), .clk(Clock));  // open: clr

  // Other names for the same wires on the sheet: Digits_4[3:0] = D4; Digits_3[3:0] = D3; Digits_2[3:0] = D2;
  //   Digits_1[3:0] = D1

  // Notes on the sheet:
  //   LSB
  //   MSB
endmodule

module ALU (
  input  [15:0] Input_A,
  input  [15:0] Input_B,
  input  [2:0] ALUop,
  output [15:0] Result,
  output [15:0] High,
  output Z_flag,
  output N_flag
);

  wire comparator_2_eq;
  wire [15:0] add_res, AND_res, high_res, mult_res, negator_1_out, NOT_res, OR_res, sll_res, srl_res, sub_res;

  Adder #(.width(16)) adder_1 (.a(Input_A), .b(Input_B), .out(add_res));  // open: cin, cout
  Subtractor #(.width(16)) subtractor_1 (.a(Input_A), .b(Input_B), .out(sub_res));  // open: bin, bout
  Multiplier #(.width(16)) multiplier_1 (.a(Input_A), .b(Input_B), .out(mult_res), .cout(high_res));  // open: cin
  assign AND_res = Input_A & Input_B;  // AND_Gate and_1, 16 bits wide
  assign OR_res = Input_A | Input_B;  // OR_Gate or_1, 16 bits wide
  Negator #(.width(16)) negator_1 (.in(Input_A), .out(negator_1_out));
  Shifter #(.width(16)) shifter_1 (.in(Input_A), .\dist (Input_B[3:0]), .out(sll_res));
  Shifter #(.width(16), .shift("lr")) shifter_2 (.in(Input_A), .\dist (Input_B[3:0]), .out(srl_res));
  Subtractor #(.width(16)) subtractor_2 (.a(negator_1_out), .b(16'h1), .out(NOT_res));  // open: bin, bout
  Comparator #(.width(16)) comparator_1 (.a(Result), .b({16{1'b0}}), .eq(Z_flag), .lt(N_flag));  // open: gt
  Comparator #(.width(3)) comparator_2 (.a(ALUop), .b(3'b010), .eq(comparator_2_eq));  // open: gt, lt
  Multiplexer #(.width(16)) multiplexer_1 (
    .in0({16{1'b0}}), .in1(high_res), .out(High), .sel(comparator_2_eq));  // open: en
  Multiplexer #(.select(3), .width(16)) multiplexer_2 (
    .in0(add_res), .in1(sub_res), .in2(mult_res), .in3(AND_res), .in4(OR_res), .in5(NOT_res), .in6(sll_res),
    .in7(srl_res), .out(Result), .sel(ALUop));  // open: en

  // Other names for the same wires on the sheet: Negative = N_flag; Operation[2:0] = ALUop; Zero = Z_flag

  // Notes on the sheet:
  //   Note: it is fine if the ALU produces a negative result we multipying two large numbers,  
  //   BUT the negative number should not be stored (see the "ALU operations" section of the ISA page for more details)
endmodule

module Register_File (
  input  [15:0] Data,
  input  I_Type,
  input  incr7,
  input  decr7,
  input  Clock,
  input  Write_Enable,
  input  [2:0] rd,
  input  [2:0] rs,
  input  [2:0] rt,
  output [15:0] rs_out,
  output [15:0] rt_out,
  output [15:0] rd_out,
  output [15:0] r7
);

  wire or_1_out, WE0, WE1, WE2, WE3, WE4, WE5, WE6, WE7;
  wire [15:0] adder_1_out, multiplexer_1_out, multiplexer_2_out, multiplexer_4_out, multiplexer_5_out, reg0,
       reg1, reg2, reg3, reg4, reg5, reg6, register_8_q, subtractor_1_out, subtractor_2_out;

  Demultiplexer #(.select(3)) demultiplexer_1 (
    .out0(WE0), .out1(WE1), .out2(WE2), .out3(WE3), .out4(WE4), .out5(WE5), .out6(WE6), .out7(WE7),
    .in(Write_Enable), .sel(rd));  // open: en
  Adder #(.width(16)) adder_1 (.a(register_8_q), .b(16'h1), .out(adder_1_out));  // open: cin, cout
  Multiplexer #(.width(16)) multiplexer_1 (
    .in0(Data), .in1(adder_1_out), .out(multiplexer_1_out), .sel(incr7));  // open: en
  Subtractor #(.width(16)) subtractor_1 (.a(register_8_q), .b(16'h1), .out(subtractor_1_out));  // open: bin, bout
  Multiplexer #(.width(16)) multiplexer_2 (
    .in0(multiplexer_1_out), .in1(subtractor_1_out), .out(multiplexer_2_out), .sel(decr7));  // open: en
  or or_1 (or_1_out, incr7, decr7, WE7);
  Register #(.width(16)) register_1 (.D(Data), .en(WE0), .Q(reg0), .clk(Clock));  // open: clr
  Register #(.width(16)) register_2 (.D(Data), .en(WE1), .Q(reg1), .clk(Clock));  // open: clr
  Register #(.width(16)) register_3 (.D(Data), .en(WE2), .Q(reg2), .clk(Clock));  // open: clr
  Register #(.width(16)) register_4 (.D(Data), .en(WE3), .Q(reg3), .clk(Clock));  // open: clr
  Register #(.width(16)) register_5 (.D(Data), .en(WE4), .Q(reg4), .clk(Clock));  // open: clr
  Register #(.width(16)) register_6 (.D(Data), .en(WE5), .Q(reg5), .clk(Clock));  // open: clr
  Register #(.width(16)) register_7 (.D(Data), .en(WE6), .Q(reg6), .clk(Clock));  // open: clr
  Register #(.width(16)) register_8 (.D(multiplexer_2_out), .en(or_1_out), .Q(register_8_q), .clk(Clock));  // open: clr
  Multiplexer #(.width(16)) multiplexer_3 (
    .in0(register_8_q), .in1(subtractor_2_out), .out(r7), .sel(decr7));  // open: en
  Subtractor #(.width(16)) subtractor_2 (.a(register_8_q), .b(16'h1), .out(subtractor_2_out));  // open: bin, bout
  Multiplexer #(.select(3), .width(16)) multiplexer_4 (
    .in0(reg0), .in1(reg1), .in2(reg2), .in3(reg3), .in4(reg4), .in5(reg5), .in6(reg6), .in7(r7),
    .out(multiplexer_4_out), .sel(rs));  // open: en
  Multiplexer #(.select(3), .width(16)) multiplexer_5 (
    .in0(reg0), .in1(reg1), .in2(reg2), .in3(reg3), .in4(reg4), .in5(reg5), .in6(reg6), .in7(r7),
    .out(multiplexer_5_out), .sel(rd));  // open: en
  Multiplexer #(.select(3), .width(16)) multiplexer_6 (
    .in0(reg0), .in1(reg1), .in2(reg2), .in3(reg3), .in4(reg4), .in5(reg5), .in6(reg6), .in7(r7),
    .out(rt_out), .sel(rt));  // open: en
  Multiplexer #(.width(16)) multiplexer_7 (
    .in0(multiplexer_4_out), .in1(multiplexer_5_out), .out(rs_out), .sel(I_Type));  // open: en
  Multiplexer #(.select(3), .width(16)) multiplexer_8 (
    .in0(reg0), .in1(reg1), .in2(reg2), .in3(reg3), .in4(reg4), .in5(reg5), .in6(reg6), .in7(r7),
    .out(rd_out), .sel(rd));  // open: en

  // Other names for the same wires on the sheet: reg7[15:0] = r7
endmodule

module PC (
  input  Halt,
  input  Clock,
  input  [1:0] PCSrc,
  input  [15:0] j_target,
  input  [7:0] immediate,
  input  N_flag,
  input  Z_flag,
  input  [2:0] branchType,
  input  [2:0] rd,
  output [15:0] PC_1,
  output [15:0] PC
);

  wire b_Length, comparator_1_eq, not_1_out, not_2_out, not_3_out, not_4_out;
  wire [1:0] flags_q;
  wire [15:0] adder_1_out, bit_extender_1_out, multiplexer_1_out, multiplexer_2_out;

  assign bit_extender_1_out = {{8{immediate[7]}}, immediate};  // Bit_Extender bit_extender_1
  Adder #(.width(16)) adder_1 (.a(PC_1), .b(bit_extender_1_out), .out(adder_1_out));  // open: cin, cout
  Multiplexer #(.width(16)) multiplexer_1 (
    .in0(PC_1), .in1(adder_1_out), .out(multiplexer_1_out), .sel(b_Length));  // open: en
  Register #(.width(2)) flags (.D({N_flag, Z_flag}), .Q(flags_q), .clk(Clock));  // open: en, clr
  Multiplexer #(.select(2), .width(16)) multiplexer_2 (
    .in0(PC_1), .in1(multiplexer_1_out), .in2(j_target), .out(multiplexer_2_out), .sel(PCSrc));  // open: in3, en
  Comparator #(.width(3)) comparator_1 (.a(rd), .b(3'b000), .eq(comparator_1_eq));  // open: gt, lt
  Register #(.width(16)) u_PC (.D(multiplexer_2_out), .en(not_1_out), .Q(PC), .clk(Clock));  // open: clr
  not not_1 (not_1_out, Halt);
  Adder #(.width(16)) adder_2 (.a(16'h1), .b(PC), .out(PC_1));  // open: cin, cout
  not not_2 (not_2_out, flags_q[1]);
  not not_3 (not_3_out, flags_q[0]);
  not not_4 (not_4_out, comparator_1_eq);
  Multiplexer #(.select(3)) multiplexer_3 (
    .in0(1'b1), .in1(not_2_out), .in2(flags_q[1]), .in3(not_3_out), .in4(flags_q[0]), .in5(comparator_1_eq),
    .in6(not_4_out), .out(b_Length), .sel(branchType));  // open: in7, en

  // Other names for the same wires on the sheet: zero = Z_flag; negative = N_flag; imm[7:0] = immediate

  // Notes on the sheet:
  //   One instruction = 16 bits
  //   Six types of conditional branches: beq, bne, blt, ble, bgt, bge 
  //   Four of the six conditional branches use previous comparison instructions: blt, ble, bgt, bge
endmodule

module Control (
  input  [15:0] ROM_out,
  output i_type,
  output [2:0] rd,
  output [2:0] rs,
  output [2:0] rt,
  output [7:0] imm,
  output halt,
  output put,
  output clr,
  output li,
  output lui,
  output mov,
  output mfhi,
  output mflo,
  output mac,
  output pop,
  output decr7,
  output incr7,
  output Signed,
  output [2:0] ALUop,
  output RegFile_WE,
  output [1:0] PCSrc,
  output [2:0] BranchType,
  output [2:0] RDS,
  output RAM_str
);

  wire add, adi, \and , ani, b, beq, bez, bge, blt, bne, bnz, call, cmp, cpi, jr, ld, mul, \not , not_1_out,
       \or , or_2_out, or_3_out, or_4_out, or_5_out, or_6_out, or_7_out, ori, push, ret, sli, sll, sri, srl,
       st, sub;

  // OR_Gate or_1 has open pins: in0=add, in1=adi, out=open
  or or_2 (or_2_out, sub, cmp, cpi);
  or or_3 (or_3_out, mul, mac);
  or or_4 (or_4_out, \and , ani);
  or or_5 (or_5_out, \or , ori);
  or or_6 (or_6_out, sll, sli);
  or or_7 (or_7_out, srl, sri);
  Priority_Encoder #(.select(2)) priority_encoder_1 (
    .in0(1'b1), .in1(jr), .in2(ret), .in3(b), .out(PCSrc));  // open: gs, en_out, en_in
  Priority_Encoder priority_encoder_2 (
    .in0(1'b1), .in1(or_2_out), .in2(or_3_out), .in3(or_4_out), .in4(or_5_out), .in5(\not ), .in6(or_6_out),
    .in7(or_7_out), .out(ALUop));  // open: en_in, gs, en_out
  or or_8 (RAM_str, st, push, call);
  or or_9 (decr7, push, call);
  or or_10 (incr7, pop, ret);
  Priority_Encoder priority_encoder_3 (
    .in0(1'b1), .in1(li), .in2(lui), .in3(mov), .in4(mfhi), .in5(mflo), .in6(ld), .in7(pop), .out(RDS));  // open: en_in, gs, en_out
  or or_11 (Signed, adi, cpi);
  Priority_Encoder priority_encoder_4 (
    .in0(1'b1), .in1(blt), .in2(bge), .in3(beq), .in4(bne), .in5(bez), .in6(bnz), .out(BranchType));  // open: in7, en_in, gs, en_out
  Demultiplexer #(.select(4)) demultiplexer_1 (
    .out0(li), .out1(lui), .out2(adi), .out3(ani), .out4(ori), .out5(sli), .out6(sri), .out7(cpi), .out8(b),
    .out9(blt), .out10(bge), .out11(beq), .out12(bne), .out13(bez), .out14(bnz), .out15(call),
    .in(ROM_out[15]), .sel(ROM_out[14:11]));  // open: en
  or or_12 (RegFile_WE, li, lui, mov, mfhi, mflo, ld, add, adi, sub, cmp, cpi, mul, mac, \and , ani, \or , ori, \not , sll, sli, srl, sri);
  Demultiplexer #(.select(5)) demultiplexer_2 (
    .out0(halt), .out1(put), .out2(clr), .out3(mov), .out4(mfhi), .out5(mflo), .out6(ld), .out7(st),
    .out8(push), .out9(pop), .out10(add), .out11(sub), .out12(cmp), .out13(mul), .out14(mac), .out15(\and ),
    .out16(\or ), .out17(\not ), .out18(sll), .out19(srl), .out20(jr), .out21(ret), .in(not_1_out),
    .sel(ROM_out[13:9]));  // open: out22, out23, out24, out25, out26, out27, out28, out29, out30, out31, en
  not not_1 (not_1_out, ROM_out[15]);

  assign i_type = ROM_out[15];
  assign imm = ROM_out[10:3];
  assign rd = ROM_out[2:0];
  assign rs = ROM_out[8:6];
  assign rt = ROM_out[5:3];

  // Other names for the same wires on the sheet: minus_r7 = decr7; plus_r7 = incr7; RegDataSrc[2:0] = RDS;
  //   i_imm[7:0] = ROM_out[10:3]; r_rt[2:0] = ROM_out[5:3]; r_rs[2:0] = ROM_out[8:6]; r_op[4:0] = ROM_out[13:9];
  //   i_op[3:0] = ROM_out[14:11]; top = ROM_out[15]

  // Notes on the sheet:
  //   rs = register source
  //   rd = register destination
endmodule
